// Logisim project s-mips.circ as structural Verilog: 10 circuits, main circuit S-MIPS Board
module S_MIPS_Board (
  input  DESHABILITAR_DISPATCHER,
  input  [31:0] Instruction_from_Mem,
  output halt
);

  wire Asrc, button_1_out, CLK, CS, d_ff_2_p1, LCLR, LoadRAM, LoadRAMOn, LW, MtR, R_R_W, R_W,
       ram_dispatcher_1_finished, RCS, RDest, Reset_out, RST, Rw, TTY_EN;
  wire [2:0] KDB;
  wire [3:0] AControl, LMask, Mask, ram_1_read_time, ram_1_write_time, RMask;
  wire [4:0] Write_Reg;
  wire [6:0] KDB_DATA, TTY_DATA;
  wire [15:0] Addr, LAddr, RAddr, undriven;
  wire [31:0] AOut, B, Data_from_Mem, I0, I1, I2, I3, Ime, LData, ram_1_data_out_0, ram_1_data_out_1,
       ram_1_data_out_2, ram_1_data_out_3, RD1, RD2, RI0, RI1, RI2, RI3, WD;
  wire [31:1] s_mips_1_kbd_clear;

  TTY #(.rows(25), .cols(80)) tty_1 (.data(TTY_DATA), .clk(CLK), .we(TTY_EN), .clr(RST));
  Register #(.width(32)) Register_Lo ();  // open: D, en, Q, clk, clr
  not not_1 (LoadRAMOn, ram_dispatcher_1_finished);
  RAM_Dispatcher ram_dispatcher_1 (
    .WriteTime_2(ram_1_write_time), .Clock(CLK), .Data(LData), .Address(LAddr), .Mask(LMask),
    .Finished(ram_dispatcher_1_finished), .Write(LW), .CLR_2(LCLR));
  Keyboard #(.buflen(64)) keyboard_1 (.clk(CLK), .re(KDB[0]), .avail(KDB[2]), .data(KDB_DATA));  // open: clr
  Register #(.width(32)) Register_Hi ();  // open: D, en, Q, clk, clr
  Program_Counter program_counter_1 ();  // open: in_1, in_2, in_3, in_4
  RAM ram_1 (
    .Address(RAddr), .Data_Out_0(ram_1_data_out_0), .Data_Out_1(ram_1_data_out_1),
    .Data_Out_2(ram_1_data_out_2), .Data_Out_3(ram_1_data_out_3), .Data_In_0(RI0), .Data_In_1(RI1),
    .Data_In_2(RI2), .Data_In_3(RI3), .Mask(RMask), .nRead_Write(R_R_W), .Chip_Select(RCS),
    .Read_Time(ram_1_read_time), .Reset(button_1_out), .Write_Time(ram_1_write_time));
  RegisterFiles registerfiles_1 (
    .Read_Register_1_2(Instruction_from_Mem[25:21]), .Read_Register_2(Instruction_from_Mem[20:16]),
    .Write_Register(Write_Reg), .RegWrite(Rw), .Clock(CLK), .Reset(RST), .Write_Data(WD), .Read_Data_1(RD1),
    .Read_Data_2(RD2));
  Button button_1 (.out(button_1_out));
  D_Flip_Flop d_ff_1 (.clk(CLK), .D(1'b1), .Q(CLK), .reset(Reset_out));  // open: Qn, preset, en
  Button Reset (.out(Reset_out));
  S_MIPS s_mips_1 (
    .Kbd_Enable(KDB[0]), .Address(Addr), .Kbd_Clear({s_mips_1_kbd_clear, KDB[1]}), .Kbd_Available(KDB[2]),
    .Kbd_Available_2(I0), .Kbd_ASCII_Data(KDB_DATA), .RAM_In_1(I1), .TTY_Enable_2(TTY_EN), .RAM_In_2(I2),
    .RAM_In_3(I3), .TTY_ASCII_Data(TTY_DATA), .Reset_2(RST), .RAM_Out_0(ram_1_data_out_0), .Clock(CLK),
    .RAM_Out_1(ram_1_data_out_1), .Stop(halt), .RAM_Out_2(ram_1_data_out_2), .RAM_Out_3(ram_1_data_out_3),
    .Mask_2(Mask), .Read_Time_2(ram_1_read_time), .Write_Time(ram_1_write_time), .nRead_Write(R_W),
    .Chip_Select(CS));
  // D_Flip_Flop d_ff_2: pin names not known; wires that end beside it: d_ff_2_p1, d_ff_2_p1, Reset_out, LCLR
  or or_1 (RST, LCLR, LoadRAM);
  assign Ime = {{16{1'b0}}, Instruction_from_Mem[15:0]};  // Bit_Extender bit_extender_1
  ALU alu_1 (.A(RD1), .B(B), .ALUControl(AControl), .Output(AOut));
  Multiplexer #(.width(32), .enable("false")) multiplexer_1 (.in0(AOut), .in1(Data_from_Mem), .out(WD), .sel(MtR));
  Clock clock_1 (.out(CLK));
  ControlUnit controlunit_1 (
    .Instruction(Instruction_from_Mem), .ALUControl(AControl), .RegWire(Rw), .MemToReg(MtR), .ALUSrc(Asrc),
    .RegDest(RDest));  // open: MemRead, MemWrite, Branch, Jump
  Multiplexer #(.width(32), .enable("false")) multiplexer_2 (.in0(RD2), .in1(Ime), .out(B), .sel(Asrc));
  Multiplexer #(.width(5), .enable("false")) multiplexer_3 (
    .in0(Instruction_from_Mem[15:11]), .in1(Instruction_from_Mem[20:16]), .out(Write_Reg), .sel(RDest));
  Multiplexer #(.width(32), .enable("false")) multiplexer_4 (.in0(I0), .in1(LData), .out(RI0), .sel(LoadRAM));
  Multiplexer #(.width(32), .enable("false")) multiplexer_5 (.in0(I1), .in1(LData), .out(RI1), .sel(LoadRAM));
  Multiplexer #(.width(32), .enable("false")) multiplexer_6 (.in0(I2), .in1(LData), .out(RI2), .sel(LoadRAM));
  Multiplexer #(.width(32), .enable("false")) multiplexer_7 (.in0(I3), .in1(LData), .out(RI3), .sel(LoadRAM));
  and and_1 (LoadRAM, ~DESHABILITAR_DISPATCHER, LoadRAMOn);  // AND_Gate
  Multiplexer #(.width(16), .enable("false")) multiplexer_8 (.in0(Addr), .in1(undriven), .out(RAddr), .sel(LoadRAM));
  Multiplexer #(.width(4), .enable("false")) multiplexer_9 (.in0(Mask), .in1(LMask), .out(RMask), .sel(LoadRAM));
  Multiplexer #(.enable("false")) multiplexer_10 (.in0(CS), .in1(LW), .out(RCS), .sel(LoadRAM));
  Multiplexer #(.enable("false")) multiplexer_11 (.in0(R_W), .in1(LW), .out(R_R_W), .sel(LoadRAM));
  // Pins of 1 and 32 bits meet at {s_mips_1_kbd_clear, KDB[1]}

  // Other names for the same wires on the sheet: InstFromMem[31:0] = Instruction_from_Mem;
  //   Inst_RD[4:0] = Instruction_from_Mem[15:11]; Inst_RT[4:0] = Instruction_from_Mem[20:16];
  //   Inst_RS[4:0] = Instruction_from_Mem[25:21]

  // Notes on the sheet:
  //   NO MODIFICAR
  //   Keyboard
  //   Output
endmodule

module RAM (
  input  [15:0] Address,
  input  [31:0] Data_In_0,
  input  [31:0] Data_In_1,
  input  [31:0] Data_In_2,
  input  [31:0] Data_In_3,
  input  [3:0] Mask,
  input  nRead_Write,
  input  Chip_Select,
  input  Reset,
  output [31:0] Data_Out_0,
  output [31:0] Data_Out_1,
  output [31:0] Data_Out_2,
  output [31:0] Data_Out_3,
  output [3:0] Read_Time,
  output [3:0] Write_Time
);

  wire and_2_out, and_3_out, and_4_out, and_5_out, and_6_out, and_7_out, and_8_out, and_9_out, Changed, CLK,
       comparator_2_eq, comparator_3_eq, comparator_4_eq, comparator_5_eq, comparator_6_eq, Count,
       demultiplexer_4_out0, Idle, Idle_q, Load, Load0, Load1, nand_1_out, or_1_out, or_2_out, or_3_out,
       or_4_out, or_5_out, or_6_out, or_7_out, or_8_out, or_9_out, or_10_out, Proc_q, undriven, Update_Mem,
       Zero_Time;
  wire [3:0] counter_1_q, Mask_t, multiplexer_1_out, subtractor_1_out;
  wire [31:0] register_1_q, register_2_q, register_3_q, register_4_q, register_5_q;
  wire [31:4] RT;

  // Probe on {RT, 4'b0011}
  // Probe on 4'b0010
  Multiplexer #(.width(4), .enable("false")) multiplexer_1 (
    .in0(4'b0011), .in1(Mask_t), .out(multiplexer_1_out), .sel(nRead_Write));
  or or_1 (or_1_out, Idle, Update_Mem);
  or or_2 (or_2_out, ~Chip_Select, Reset);  // OR_Gate
  Subtractor #(.width(4)) subtractor_1 (.a(multiplexer_1_out), .b(4'b0010), .out(subtractor_1_out));  // open: bin, bout
  Demultiplexer #(.enable("false")) demultiplexer_1 (.out0(Idle), .out1(Load0), .in(Idle_q), .sel(Changed));
  D_Flip_Flop u_Idle (.clk(CLK), .D(or_1_out), .Q(Idle_q), .preset(or_2_out));  // open: Qn, en, reset
  Demultiplexer #(.enable("false")) demultiplexer_2 (.out0(Idle), .out1(Load0), .in(Idle_q), .sel(Changed));
  // Probe on counter_1_q
  Counter #(.width(4), .max('hf)) counter_1 (
    .load(Load), .D(subtractor_1_out), .count(Count), .Q(counter_1_q), .clk(CLK), .clr(or_3_out));  // open: carry
  or or_3 (or_3_out, ~Chip_Select, Reset);  // OR_Gate
  Comparator #(.width(4), .mode("unsigned")) comparator_1 (
    .a(4'b0000), .b(counter_1_q), .eq(Zero_Time));  // open: gt, lt
  or or_4 (or_4_out, Count, Load0, Load1);
  Register #(.width(32)) register_1 (.D(Data_In_0), .en(Chip_Select), .Q(register_1_q), .clk(CLK), .clr(or_5_out));
  or or_5 (or_5_out, ~Chip_Select, Reset);  // OR_Gate
  Register #(.width(32)) register_2 (.D(Data_In_1), .en(Chip_Select), .Q(register_2_q), .clk(CLK), .clr(or_6_out));
  or or_6 (or_6_out, ~Chip_Select, Reset);  // OR_Gate
  Register #(.width(32)) register_3 (.D(Data_In_2), .en(Chip_Select), .Q(register_3_q), .clk(CLK), .clr(or_7_out));
  or or_7 (or_7_out, ~Chip_Select, Reset);  // OR_Gate
  Register #(.width(32)) register_4 (.D(Data_In_3), .en(Chip_Select), .Q(register_4_q), .clk(CLK), .clr(or_8_out));
  or or_8 (or_8_out, ~Chip_Select, Reset);  // OR_Gate
  Register #(.width(32)) register_5 (
    .D({{11{1'b1}}, nRead_Write, Mask, Address}), .en(Chip_Select), .Q(register_5_q), .clk(CLK),
    .clr(or_9_out));
  or or_9 (or_9_out, ~Chip_Select, undriven);  // OR_Gate
  D_Flip_Flop Proc (.clk(CLK), .D(or_4_out), .Q(Proc_q), .reset(or_10_out));  // open: Qn, preset, en
  or or_10 (or_10_out, ~Chip_Select, Reset);  // OR_Gate
  Demultiplexer #(.enable("false")) demultiplexer_3 (
    .out0(Count), .out1(Update_Mem), .in(demultiplexer_4_out0), .sel(Zero_Time));
  Demultiplexer #(.enable("false")) demultiplexer_4 (
    .out0(demultiplexer_4_out0), .out1(Load1), .in(Proc_q), .sel(Changed));
  Clock clock_1 (.out(CLK));
  Comparator #(.width(32)) comparator_2 (.a(register_1_q), .b(Data_In_0), .eq(comparator_2_eq));  // open: gt, lt
  Comparator #(.width(32)) comparator_3 (.a(register_2_q), .b(Data_In_1), .eq(comparator_3_eq));  // open: gt, lt
  Comparator #(.width(32)) comparator_4 (.a(register_3_q), .b(Data_In_2), .eq(comparator_4_eq));  // open: gt, lt
  Comparator #(.width(32)) comparator_5 (.a(register_4_q), .b(Data_In_3), .eq(comparator_5_eq));  // open: gt, lt
  Comparator #(.width(32)) comparator_6 (
    .a(register_5_q), .b({{11{1'b1}}, nRead_Write, Mask, Address}), .eq(comparator_6_eq));  // open: gt, lt
  nand nand_1 (nand_1_out, comparator_6_eq, comparator_2_eq, comparator_3_eq, comparator_4_eq, comparator_5_eq);
  and and_1 (Changed, nand_1_out, Chip_Select);
  or or_11 (Load, Count, Load1, Load0);
  and and_2 (and_2_out, Mask[0], Update_Mem, nRead_Write);
  and and_3 (and_3_out, Mask[1], Update_Mem, nRead_Write);
  and and_4 (and_4_out, Mask[2], Update_Mem, nRead_Write);
  and and_5 (and_5_out, Mask[3], Update_Mem, nRead_Write);
  RAM_part #(.addrWidth(16), .dataWidth(32), .bus("separate")) ram_1 (
    .addr(Address), .din(Data_In_0), .data(Data_Out_0), .str(and_2_out), .sel(Chip_Select), .clk(CLK),
    .ld(and_6_out), .clr(Reset));
  and and_6 (and_6_out, ~nRead_Write, Idle);  // AND_Gate
  RAM_part #(.addrWidth(16), .dataWidth(32), .bus("separate")) ram_2 (
    .addr(Address), .din(Data_In_1), .data(Data_Out_1), .str(and_3_out), .sel(Chip_Select), .clk(CLK),
    .ld(and_7_out), .clr(Reset));
  and and_7 (and_7_out, ~nRead_Write, Idle);  // AND_Gate
  RAM_part #(.addrWidth(16), .dataWidth(32), .bus("separate")) ram_3 (
    .addr(Address), .din(Data_In_2), .data(Data_Out_2), .str(and_4_out), .sel(Chip_Select), .clk(CLK),
    .ld(and_8_out), .clr(Reset));
  and and_8 (and_8_out, ~nRead_Write, Idle);  // AND_Gate
  RAM_part #(.addrWidth(16), .dataWidth(32), .bus("separate")) ram_4 (
    .addr(Address), .din({RT, 4'b0011}), .data(Data_Out_3), .str(and_5_out), .sel(Chip_Select), .clk(CLK),
    .ld(and_9_out), .clr(Reset));
  and and_9 (and_9_out, ~nRead_Write, Idle);  // AND_Gate
  // Pins of 4 and 32 bits meet at {RT, 4'b0011}

  assign Read_Time = 4'b0011;
  assign Write_Time = 4'b0010;

  // Other names for the same wires on the sheet: M0 = Mask[0]; M1 = Mask[1]; M2 = Mask[2]; M3 = Mask[3];
  //   RW = nRead_Write; CLR = Reset; CS = Chip_Select; Load2 = Count

  // Notes on the sheet:
  //   NO MODIFICAR
  //   excepto quizás los valores RT y WT
  //   BANK0
  //   BANK1
  //   BANK2
  //   BANK3
endmodule

module S_MIPS (
  input  Kbd_Available,
  input  [6:0] Kbd_ASCII_Data,
  input  [31:0] RAM_Out_0,
  input  [31:0] RAM_Out_1,
  input  Reset,
  input  Reset_2,
  input  [31:0] RAM_Out_2,
  input  Clock,
  input  [31:0] RAM_Out_3,
  input  [3:0] Read_Time,
  input  [3:0] Read_Time_2,
  input  [3:0] Write_Time,
  output Kbd_Enable,
  output [15:0] Address,
  output [31:0] Kbd_Clear,
  output TTY_Enable,
  output TTY_Enable_2,
  output [6:0] TTY_ASCII_Data,
  output Stop,
  output [31:0] Kbd_Available_2,
  output [31:0] RAM_In_1,
  output [31:0] RAM_In_2,
  output [31:0] RAM_In_3,
  output [3:0] Mask,
  output [3:0] Mask_2,
  output nRead_Write,
  output Chip_Select
);

  // Pins of 1 and 32 bits meet at Kbd_Clear

  assign Mask_2 = Mask;
  assign Read_Time_2 = Read_Time;
  assign Reset_2 = Reset;
  assign TTY_Enable_2 = TTY_Enable;

  // Other names for the same wires on the sheet: CLK = Clock; CLR = Reset; CS = Chip_Select;
  //   KBD_AVAIL = Kbd_Available; KBD_CLR[31:0] = Kbd_Clear; KBD_DATA[6:0] = Kbd_ASCII_Data; RAM_A[15:0] = Address;
  //   RAM_INPUT_0[31:0] = Kbd_Available_2; RAM_INPUT_1[31:0] = RAM_In_1; RAM_INPUT_2[31:0] = RAM_In_2;
  //   RAM_INPUT_3[31:0] = RAM_In_3; RAM_OUTPUT_0[31:0] = RAM_Out_0; RAM_OUTPUT_1[31:0] = RAM_Out_1;
  //   RAM_OUTPUT_2[31:0] = RAM_Out_2; RAM_OUTPUT_3[31:0] = RAM_Out_3; RW = nRead_Write;
  //   TTY_DATA[6:0] = TTY_ASCII_Data

  // Notes on the sheet:
  //   RAM ADDRESS
  //   DATA FROM RAM
  //   DATA TO RAM
  //   DATA WRITE MASK
  //   RAM TIMING
  //   RAM CONTROL
  //   KEYBOARD
  //   TTY
  //   SEQUENCING
endmodule

module RAM_Dispatcher (
  input  [3:0] WriteTime,
  input  [3:0] WriteTime_2,
  input  Clock,
  input  CLR,
  input  CLR_2,
  output [31:0] Data,
  output [15:0] Address,
  output [3:0] Mask,
  output Finished,
  output Write
);

  wire comparator_2_gt, comparator_2_lt, counter_1_carry, demultiplexer_2_out1, demultiplexer_3_out1, End,
       IDLE_q, IDLE_qn, IncAddr, Load, or_1_out, or_3_out, undriven, undriven_2, undriven_3, undriven_4,
       undriven_5, undriven_6, undriven_7, undriven_8, While_q, While_qn, WriteEnd;
  wire [3:0] counter_1_q;
  wire [31:0] CurrentAddress_q;

  Counter #(.width(32), .max('hffffffff)) CurrentAddress (
    .count(IncAddr), .Q({CurrentAddress_q[31:18], Address, CurrentAddress_q[1:0]}), .clk(Clock), .clr(CLR));  // open: load, D, carry
  or or_1 (or_1_out, IncAddr, demultiplexer_3_out1, Finished);
  or or_2 (or_1_out, IncAddr, demultiplexer_3_out1, Finished);
  D_Flip_Flop IDLE (
    .clk(Clock), .D(or_1_out), .Q(IDLE_q), .Qn(IDLE_qn), .preset(CLR), .en(undriven), .reset(undriven_2));
  D_Flip_Flop IDLE_2 (
    .clk(Clock), .D(or_1_out), .Q(IDLE_q), .Qn(IDLE_qn), .preset(CLR), .en(undriven), .reset(undriven_2));
  Demultiplexer #(.enable("false")) demultiplexer_1 (.out0(Load), .out1(Finished), .in(IDLE_q), .sel(End));
  D_Flip_Flop While (
    .clk(Clock), .D(or_3_out), .Q(While_q), .Qn(While_qn), .preset(undriven_4), .en(undriven_5), .reset(CLR));
  D_Flip_Flop While_2 (
    .clk(Clock), .D(or_3_out), .Q(While_q), .Qn(While_qn), .preset(undriven_4), .en(undriven_5), .reset(CLR));
  or or_3 (or_3_out, Write, Load);
  or or_4 (or_3_out, Write, Load);
  RAM_part #(.addrWidth(18), .dataWidth(32)) ram_1 (
    .addr({Address, CurrentAddress_q[1:0]}), .data(Data), .sel(undriven_3), .clk(Clock), .ld(undriven_6),
    .clr(undriven_7));
  RAM_part #(.addrWidth(18), .dataWidth(32)) ram_2 (
    .addr({Address, CurrentAddress_q[1:0]}), .data(Data), .sel(undriven_3), .clk(Clock), .ld(undriven_6),
    .clr(undriven_7));
  Demultiplexer #(.enable("false")) demultiplexer_2 (
    .out0(Write), .out1(demultiplexer_2_out1), .in(While_q), .sel(WriteEnd));
  Decoder #(.select(2)) decoder_1 (
    .out0(Mask[0]), .out1(Mask[1]), .out2(Mask[2]), .out3(Mask[3]), .sel(CurrentAddress_q[1:0]));  // open: en
  Demultiplexer #(.enable("false")) demultiplexer_3 (
    .out0(IncAddr), .out1(demultiplexer_3_out1), .in(demultiplexer_2_out1), .sel(End));
  Counter #(.width(4), .max('hf)) counter_1 (
    .load(Load), .D(WriteTime), .count(Write), .Q(counter_1_q), .carry(counter_1_carry), .clk(Clock),
    .clr(undriven_8));
  Counter #(.width(4), .max('hf)) counter_2 (
    .load(Load), .D(WriteTime), .count(Write), .Q(counter_1_q), .carry(counter_1_carry), .clk(Clock),
    .clr(undriven_8));
  Comparator #(.width(32)) comparator_1 (.a(Data), .b({32{1'b1}}), .eq(End));  // open: gt, lt
  Comparator #(.width(4)) comparator_2 (
    .a(4'b0000), .b(counter_1_q), .gt(comparator_2_gt), .eq(WriteEnd), .lt(comparator_2_lt));
  Comparator #(.width(4)) comparator_3 (
    .a(4'b0000), .b(counter_1_q), .gt(comparator_2_gt), .eq(WriteEnd), .lt(comparator_2_lt));

  assign CLR_2 = CLR;
  assign WriteTime_2 = WriteTime;

  // Other names for the same wires on the sheet: CLK = Clock; Count = Write; WT[3:0] = WriteTime
endmodule

module ALU (
  input  [31:0] A,
  input  [31:0] B,
  input  [3:0] ALUControl,
  output [31:0] Output
);

  wire [31:0] adder_1_out, subtractor_1_out;

  Adder #(.width(32)) adder_1 (.a(A), .b(B), .out(adder_1_out));  // open: cin, cout
  Subtractor #(.width(32)) subtractor_1 (.a(A), .b(B), .out(subtractor_1_out));  // open: bin, bout
  Multiplexer #(.select(4), .width(32), .enable("false")) multiplexer_1 (
    .in0(adder_1_out), .in1(subtractor_1_out), .out(Output), .sel(ALUControl));  // open: in2, in3, in4, in5, in6, in7, in8, in9, in10, in11, in12, in13, in14, in15
endmodule

module RegisterFiles (
  input  [4:0] Read_Register_1,
  input  [4:0] Read_Register_1_2,
  input  [4:0] Read_Register_2,
  input  [31:0] Write_Data,
  input  [4:0] Write_Register,
  input  RegWrite,
  input  Clock,
  input  Reset,
  output [31:0] Read_Data_1,
  output [31:0] Read_Data_2
);

  wire and_1_out, and_3_out, and_4_out, and_5_out, and_6_out, and_8_out, and_10_out, and_11_out, and_12_out,
       and_13_out, and_14_out, and_16_out, and_17_out, and_18_out, and_19_out, and_20_out, and_21_out,
       and_23_out, and_24_out, and_25_out, and_26_out, and_28_out, and_30_out, and_31_out, and_32_out,
       and_33_out, and_34_out, and_35_out, and_37_out, and_38_out, and_39_out, and_41_out, D0, D1, D2, D3,
       D4, D5, D6, D7, D8, D9, D10, D11, D12, D13, D14, D15, D16, D17, D18, D19, D20, D21, D22, D23, D24,
       D25, D26, D27, D28, D29, D30, D31;
  wire [31:0] R0, R1, R2, R3, R4, R5, R6, R7, R8, R9, R10, R11, R12, R13, R14, R15, R16, R17, R18, R19, R20,
       R21, R22, R23, R24, R25, R26, R27, R28, R29, R30, R31;

  Decoder #(.select(5), .enable("false")) decoder_1 (
    .out0(D0), .out1(D1), .out2(D2), .out3(D3), .out4(D4), .out5(D5), .out6(D6), .out7(D7), .out8(D8),
    .out9(D9), .out10(D10), .out11(D11), .out12(D12), .out13(D13), .out14(D14), .out15(D15), .out16(D16),
    .out17(D17), .out18(D18), .out19(D19), .out20(D20), .out21(D21), .out22(D22), .out23(D23), .out24(D24),
    .out25(D25), .out26(D26), .out27(D27), .out28(D28), .out29(D29), .out30(D30), .out31(D31),
    .sel(Write_Register));
  Decoder #(.select(5), .enable("false")) decoder_2 (
    .out0(D0), .out1(D1), .out2(D2), .out3(D3), .out4(D4), .out5(D5), .out6(D6), .out7(D7), .out8(D8),
    .out9(D9), .out10(D10), .out11(D11), .out12(D12), .out13(D13), .out14(D14), .out15(D15), .out16(D16),
    .out17(D17), .out18(D18), .out19(D19), .out20(D20), .out21(D21), .out22(D22), .out23(D23), .out24(D24),
    .out25(D25), .out26(D26), .out27(D27), .out28(D28), .out29(D29), .out30(D30), .out31(D31),
    .sel(Write_Register));
  Multiplexer #(.select(5), .width(32), .enable("false")) multiplexer_1 (
    .in0(R0), .in1(R1), .in2(R2), .in3(R3), .in4(R4), .in5(R5), .in6(R6), .in7(R7), .in8(R8),
    .in9(Write_Data), .in10(R10), .in11(R11), .in12(R12), .in13(R13), .in14(R14), .in15(R9), .in16(R16),
    .in17(R17), .in18(R18), .in19(R19), .in20(R20), .in21(R21), .in22(R22), .in23(R23), .in24(R24),
    .in25(R25), .in26(R26), .in27(R27), .in28(R28), .in29(R29), .in30(R30), .in31(R31), .out(Read_Data_1),
    .sel(Read_Register_1));
  Multiplexer #(.select(5), .width(32), .enable("false")) multiplexer_2 (
    .in0(R0), .in1(R1), .in2(R2), .in3(R3), .in4(R4), .in5(R5), .in6(R6), .in7(R7), .in8(R8),
    .in9(Write_Data), .in10(R10), .in11(R11), .in12(R12), .in13(R13), .in14(R14), .in15(R9), .in16(R16),
    .in17(R17), .in18(R18), .in19(R19), .in20(R20), .in21(R21), .in22(R22), .in23(R23), .in24(R24),
    .in25(R25), .in26(R26), .in27(R27), .in28(R28), .in29(R29), .in30(R30), .in31(R31), .out(Read_Data_1),
    .sel(Read_Register_1));
  Multiplexer #(.select(5), .width(32), .enable("false")) multiplexer_3 (
    .in0(R0), .in1(R1), .in2(R2), .in3(R3), .in4(R4), .in5(R5), .in6(R6), .in7(R7), .in8(R8), .in9(R9),
    .in10(R10), .in11(R11), .in12(R12), .in13(R13), .in14(R14), .in15(R15), .in16(R16), .in17(R17),
    .in18(R18), .in19(R19), .in20(R20), .in21(R21), .in22(R22), .in23(R23), .in24(R24), .in25(R25),
    .in26(R26), .in27(R27), .in28(R28), .in29(R29), .in30(R30), .in31(R31), .out(Read_Data_2),
    .sel(Read_Register_2));
  and and_1 (and_1_out, D0, RegWrite);
  and and_2 (and_1_out, D0, RegWrite);
  and and_3 (and_3_out, D1, RegWrite);
  and and_4 (and_4_out, D2, RegWrite);
  and and_5 (and_5_out, D3, RegWrite);
  and and_6 (and_6_out, D8, RegWrite);
  and and_7 (and_6_out, D8, RegWrite);
  and and_8 (and_8_out, D9, RegWrite);
  and and_9 (and_8_out, D9, RegWrite);
  and and_10 (and_10_out, D10, RegWrite);
  and and_11 (and_11_out, D11, RegWrite);
  and and_12 (and_12_out, D16, RegWrite);
  and and_13 (and_13_out, D17, RegWrite);
  and and_14 (and_14_out, D18, RegWrite);
  and and_15 (and_14_out, D18, RegWrite);
  and and_16 (and_16_out, D19, RegWrite);
  and and_17 (and_17_out, D24, RegWrite);
  and and_18 (and_18_out, D25, RegWrite);
  and and_19 (and_19_out, D26, RegWrite);
  and and_20 (and_20_out, D27, RegWrite);
  Register #(.width(32)) register_1 (.D(Write_Data), .en(and_1_out), .Q(R0), .clk(Clock), .clr(Reset));
  Register #(.width(32)) register_2 (.D(Write_Data), .en(and_3_out), .Q(R1), .clk(Clock), .clr(Reset));
  Register #(.width(32)) register_3 (.D(Write_Data), .en(and_4_out), .Q(R2), .clk(Clock), .clr(Reset));
  Register #(.width(32)) register_4 (.D(Write_Data), .en(and_5_out), .Q(R3), .clk(Clock), .clr(Reset));
  Register #(.width(32)) register_5 (.D(Write_Data), .en(and_6_out), .Q(R8), .clk(Clock), .clr(Clock));
  Register #(.width(32)) register_6 (.D(Write_Data), .en(and_8_out), .Q(R9), .clk(Clock), .clr(Reset));
  Register #(.width(32)) register_7 (.D(Write_Data), .en(and_8_out), .Q(R9), .clk(Clock), .clr(Reset));
  Register #(.width(32)) register_8 (.D(Write_Data), .en(and_10_out), .Q(R10), .clk(Clock), .clr(Reset));
  Register #(.width(32)) register_9 (.D(Write_Data), .en(and_11_out), .Q(R11), .clk(Clock), .clr(Reset));
  Register #(.width(32)) register_10 (.D(Write_Data), .en(and_12_out), .Q(R16), .clk(Clock), .clr(Reset));
  Register #(.width(32)) register_11 (.D(Write_Data), .en(and_13_out), .Q(R17), .clk(Clock), .clr(Reset));
  Register #(.width(32)) register_12 (.D(Write_Data), .en(and_14_out), .Q(R18), .clk(Clock), .clr(Reset));
  Register #(.width(32)) register_13 (.D(Write_Data), .en(and_16_out), .Q(R19), .clk(Clock), .clr(Reset));
  Register #(.width(32)) register_14 (.D(Write_Data), .en(and_17_out), .Q(R24), .clk(Clock), .clr(Reset));
  Register #(.width(32)) register_15 (.D(Write_Data), .en(and_18_out), .Q(R25), .clk(Clock), .clr(Reset));
  Register #(.width(32)) register_16 (.D(Write_Data), .en(and_18_out), .Q(R25), .clk(Clock), .clr(Reset));
  Register #(.width(32)) register_17 (.D(Write_Data), .en(and_19_out), .Q(R26), .clk(Clock), .clr(Reset));
  Register #(.width(32)) register_18 (.D(Write_Data), .en(and_20_out), .Q(R27), .clk(Clock), .clr(Reset));
  and and_21 (and_21_out, D4, RegWrite);
  and and_22 (and_21_out, D4, RegWrite);
  and and_23 (and_23_out, D5, RegWrite);
  and and_24 (and_24_out, D6, RegWrite);
  and and_25 (and_25_out, D7, RegWrite);
  and and_26 (and_26_out, D12, RegWrite);
  and and_27 (and_26_out, D12, RegWrite);
  and and_28 (and_28_out, D13, RegWrite);
  and and_29 (and_28_out, D13, RegWrite);
  and and_30 (and_30_out, D14, RegWrite);
  and and_31 (and_31_out, D15, RegWrite);
  and and_32 (and_32_out, D20, RegWrite);
  and and_33 (and_33_out, D21, RegWrite);
  and and_34 (and_34_out, D22, RegWrite);
  and and_35 (and_35_out, D23, RegWrite);
  and and_36 (and_35_out, D23, RegWrite);
  and and_37 (and_37_out, D12, RegWrite);
  and and_38 (and_38_out, D13, RegWrite);
  and and_39 (and_39_out, D14, RegWrite);
  and and_40 (and_39_out, D14, RegWrite);
  and and_41 (and_41_out, D15, RegWrite);
  Register #(.width(32)) register_19 (.D(Write_Data), .en(and_21_out), .Q(R4), .clk(Clock), .clr(Reset));
  Register #(.width(32)) register_20 (.D(Write_Data), .en(and_23_out), .Q(R5), .clk(Clock), .clr(Reset));
  Register #(.width(32)) register_21 (.D(Write_Data), .en(and_24_out), .Q(R6), .clk(Clock), .clr(Reset));
  Register #(.width(32)) register_22 (.D(Write_Data), .en(and_25_out), .Q(R7), .clk(Clock), .clr(Reset));
  Register #(.width(32)) register_23 (.D(Write_Data), .en(and_25_out), .Q(R7), .clk(Clock), .clr(Reset));
  Register #(.width(32)) register_24 (.D(Write_Data), .en(and_26_out), .Q(R12), .clk(Clock), .clr(Reset));
  Register #(.width(32)) register_25 (.D(Write_Data), .en(and_28_out), .Q(R13), .clk(Clock), .clr(Reset));
  Register #(.width(32)) register_26 (.D(Write_Data), .en(and_30_out), .Q(R14), .clk(Clock), .clr(Reset));
  Register #(.width(32)) register_27 (.D(Write_Data), .en(and_31_out), .Q(R15), .clk(Clock), .clr(Reset));
  Register #(.width(32)) register_28 (.D(Write_Data), .en(and_32_out), .Q(R20), .clk(Clock), .clr(Reset));
  Register #(.width(32)) register_29 (.D(Write_Data), .en(and_33_out), .Q(R21), .clk(Clock), .clr(Reset));
  Register #(.width(32)) register_30 (.D(Write_Data), .en(and_34_out), .Q(R22), .clk(Clock), .clr(Reset));
  Register #(.width(32)) register_31 (.D(Write_Data), .en(and_35_out), .Q(R23), .clk(Clock), .clr(Reset));
  Register #(.width(32)) u_R13 (.D(Write_Data), .en(and_37_out), .Q(R12), .clk(Clock), .clr(Reset));
  Register #(.width(32)) register_32 (.D(Write_Data), .en(and_38_out), .Q(R13), .clk(Clock), .clr(Reset));
  Register #(.width(32)) register_33 (.D(Write_Data), .en(and_39_out), .Q(R14), .clk(Clock), .clr(Reset));
  Register #(.width(32)) register_34 (.D(Write_Data), .en(and_41_out), .Q(R15), .clk(Clock), .clr(Reset));

  assign Read_Register_1_2 = Read_Register_1;

  // Other names for the same wires on the sheet: CLK = Clock; RD1[31:0] = Read_Data_1; RD2[31:0] = Read_Data_2;
  //   RE = Reset; RR1[4:0] = Read_Register_1; RR2[4:0] = Read_Register_2; RW = RegWrite; WD[31:0] = Write_Data;
  //   WR[4:0] = Write_Register

  // Notes on the sheet:
  //   READING
  //   WRITING
  //   WRITING
  //   OTHERS
  //   OTHERS
  //   IMPUTS
  //   SENDING THE DATA
  //   SENDING THE DATA
  //   OUTPUTS
  //   READING DATA
  //   SELECTING READING REGISTERS
  //   SECTION 1
  //   SECTION 2
  //   0 - 15
  //   16 - 31
  //   16 - 31
endmodule

module Program_Counter (
  input  [31:0] in_1,
  input  in_2,
  input  in_3,
  input  in_4
);

  wire [31:0] register_1_q;

  Register #(.width(32)) register_1 (.D(in_1), .en(in_3), .Q(register_1_q), .clk(in_4), .clr(in_2));
  Register #(.width(32)) register_2 (.D(in_1), .en(in_3), .Q(register_1_q), .clk(in_4), .clr(in_2));

  // Other names for the same wires on the sheet: clk = in_4; enable = in_3; PC_prime[31:0] = in_1; reset = in_2

  // Notes on the sheet:
  //   Input
  //   Processing Data
  //   Output
endmodule

module Branch_Control (
  input  [2:0] in_1,
  input  in_2,
  input  in_3,
  input  [31:0] in_4,
  input  [25:0] in_5,
  input  [31:0] in_6,
  input  [31:0] in_7,
  output [31:0] PC_prime
);

  wire and_1_out, and_2_out, and_3_out, and_4_out, and_5_out, and_6_out, and_7_out, beq, bgtz, blez, bltz,
       bne, cond, j, jr, nop, or_1_out;
  wire [1:0] jump_select;
  wire [31:0] multiplier_1_out, PC_4, PC_4_offset_4;

  or or_1 (or_1_out, in_3, in_2);
  and and_1 (and_1_out, ~in_3, ~in_2);  // AND_Gate
  and and_2 (and_2_out, ~in_3, in_2);  // AND_Gate
  and and_3 (and_3_out, beq, in_3);
  and and_4 (and_4_out, bne, ~in_3);  // AND_Gate
  and and_5 (and_5_out, blez, or_1_out);
  and and_6 (and_6_out, bgtz, and_1_out);
  and and_7 (and_7_out, bltz, and_2_out);
  or or_2 (cond, and_3_out, and_4_out, and_5_out, and_6_out, and_7_out);
  Adder #(.width(32)) adder_1 (.a(in_4), .b(32'h4), .out(PC_4));  // open: cin, cout
  Multiplexer #(.select(2), .width(32), .enable("false")) multiplexer_1 (
    .in0(PC_4), .in1(PC_4_offset_4), .in2({in_4[31:28], in_5, 2'b00}), .in3(in_6), .out(PC_prime),
    .sel(jump_select));
  Multiplier #(.width(32)) multiplier_1 (.a(32'h4), .b(in_7), .out(multiplier_1_out));  // open: cin, cout
  Adder #(.width(32)) adder_2 (.a(PC_4), .b(multiplier_1_out), .out(PC_4_offset_4));  // open: cin, cout
  Decoder #(.select(3), .enable("false")) decoder_1 (
    .out0(nop), .out1(beq), .out2(bne), .out3(blez), .out4(bgtz), .out5(bltz), .out6(j), .out7(jr), .sel(in_1));
  Priority_Encoder #(.select(2)) priority_encoder_1 (
    .in0(1'b1), .in1(cond), .in2(j), .in3(jr), .out(jump_select), .en_in(1'b1));  // open: gs, en_out

  // Other names for the same wires on the sheet: destino[31:2] = {in_4[31:28], in_5}; jump_size[25:0] = in_5;
  //   PC[31:0] = in_4; offset[31:0] = in_7; RS[31:0] = in_6; select_jump_type[2:0] = in_1; sing_flag = in_2;
  //   zero_flag = in_3

  // Notes on the sheet:
  //   Inputs
  //   Checking Conditon
  //   Output
  //   Processing Data
  //   Select the Jump Type
  //   Select the Jump
endmodule

module ControlUnit (
  input  [31:0] Instruction,
  output [3:0] ALUControl,
  output RegWire,
  output MemRead,
  output MemWrite,
  output MemToReg,
  output ALUSrc,
  output RegDest,
  output Branch,
  output Jump
);

  wire comparator_1_eq, is_addi;
  wire [1:1] AOP;
  wire [3:0] aludecoder_1_p2;
  wire [5:0] FunCode, OpCode;

  Comparator #(.width(6)) comparator_1 (.a(OpCode), .b({6{1'b0}}), .eq(comparator_1_eq));  // open: gt, lt
  Comparator #(.width(6)) comparator_2 (.a(OpCode), .b(6'b100011), .eq(MemRead));  // open: gt, lt
  Comparator #(.width(6)) comparator_3 (.a(OpCode), .b(6'b101011), .eq(MemWrite));  // open: gt, lt
  Comparator #(.width(6)) comparator_4 (.a(OpCode), .b(6'b001000), .eq(is_addi));  // open: gt, lt
  Comparator #(.width(6)) comparator_5 (.a(OpCode), .b(6'b000100), .eq(Branch));  // open: gt, lt
  Comparator #(.width(6)) comparator_6 (.a(OpCode), .b(6'b000010), .eq(Jump));  // open: gt, lt
  // ALUDecoder aludecoder_1: pin names not known; wires that end beside it: FunCode, aludecoder_1_p2
  Multiplexer #(.select(2), .width(4), .enable("false")) multiplexer_1 (
    .in0(4'b0000), .in1(4'b0001), .in2(aludecoder_1_p2), .out(ALUControl), .sel({AOP[1], Branch}));  // open: in3
  or or_1 (RegWire, AOP[1], MemRead, is_addi);
  or or_2 (ALUSrc, MemRead, MemWrite);
  or or_3 (RegDest, MemRead, is_addi);

  assign MemToReg = MemRead;

  // Other names for the same wires on the sheet: AC[3:0] = ALUControl; AOP[0] = Branch; Bch = Branch; is_beq = Branch;
  //   is_R = AOP[1]; ASrc = ALUSrc; INST[31:0] = Instruction; is_jmp = Jump; Jmp = Jump; is_lw = MemRead;
  //   MR = MemRead; MtR = MemRead; is_sw = MemWrite; MW = MemWrite; RDest = RegDest; RW = RegWire

  // Notes on the sheet:
  //   IMPUTS
  //   OUTPUTS
  //   ALUDecoder
  //   OpCode
  //   000000
  //   is R type
  //   100011
  //   100011
  //   is lw
  //   101011
  //   101011
  //   is sw
  //   001000
  //   is addi
  //   000100
  //   000100
  //   is beq
  //   000010
  //   is jmp
  //   RegWire
  //   MemoryRead
  //   Branch
  //   Jump
  //   Jump
  //   MemoryWrite
  //   MemoryToReg
  //   ALUSrc
  //   Register Destination
endmodule

module ALUDecoder (
  input  [5:0] FunCode,
  output [3:0] ALUControl
);

  wire add, \and , bit_3, comparator_2_gt, comparator_2_lt, div, divu, mult, mulu, \not , \or , slt, sltu,
       sub, \xor ;

  Comparator #(.width(6)) comparator_1 (.a(FunCode), .b(6'b100000), .eq(add));  // open: gt, lt
  Comparator #(.width(6)) comparator_2 (
    .a(FunCode), .b(6'b100010), .gt(comparator_2_gt), .eq(sub), .lt(comparator_2_lt));
  Comparator #(.width(6)) comparator_3 (
    .a(FunCode), .b(6'b100010), .gt(comparator_2_gt), .eq(sub), .lt(comparator_2_lt));
  Comparator #(.width(6)) comparator_4 (.a(FunCode), .b(6'b011000), .eq(mult));  // open: gt, lt
  Comparator #(.width(6)) comparator_5 (.a(FunCode), .b(6'b011001), .eq(mulu));  // open: gt, lt
  Comparator #(.width(6)) comparator_6 (.a(FunCode), .b(6'b011010), .eq(div));  // open: gt, lt
  Comparator #(.width(6)) comparator_7 (.a(FunCode), .b(6'b011011), .eq(divu));  // open: gt, lt
  Comparator #(.width(6)) comparator_8 (.a(FunCode), .b(6'b100100), .eq(\and ));  // open: gt, lt
  Comparator #(.width(6)) comparator_9 (.a(FunCode), .b(6'b100101), .eq(\or ));  // open: gt, lt
  Comparator #(.width(6)) comparator_10 (.a(FunCode), .b(6'b100111), .eq(\not ));  // open: gt, lt
  Comparator #(.width(6)) comparator_11 (.a(FunCode), .b(6'b101000), .eq(\xor ));  // open: gt, lt
  Comparator #(.width(6)) comparator_12 (.a(FunCode), .b(6'b101010), .eq(slt));  // open: gt, lt
  Comparator #(.width(6)) comparator_13 (.a(FunCode), .b(6'b101011), .eq(sltu));  // open: gt, lt
  or or_1 (ALUControl[0], sub, mulu, divu, \or , \xor , sltu);
  or or_2 (ALUControl[1], mult, mulu, \and , \or , slt, sltu);
  or or_3 (ALUControl[2], div, divu, \and , \or );
  or or_4 (bit_3, \not , \xor , slt, sltu);

  // Other names for the same wires on the sheet: AC[3:0] = ALUControl; bit_0 = ALUControl[0]; bit_1 = ALUControl[1];
  //   bit_2 = ALUControl[2]; FC[5:0] = FunCode

  // Notes on the sheet:
  //   IMPUTS
  //   100000
  //   100010
  //   011000
  //   011001
  //   011010
  //   011011
  //   100100
  //   is Add
  //   is Sub
  //   is mult
  //   is mulu
  //   is div
  //   is divu
  //   is and
  //   100101
  //   is or
  //   100111
  //   is not
  //   101000
  //   is xor
  //   101010
  //   is slt
  //   101011
  //   is sltu
  //   0000
  //   0001
  //   0010
  //   0011
  //   0100
  //   0101
  //   0110
  //   0111
  //   1000
  //   1001
  //   1010
  //   1011
  //   OUTPUTS
endmodule
